# Fritzing sketch RFMX9HCW_QT_XIAO_Backpack_v1 (saved by Fritzing 0.9.3b)
circuit board: 2cm x 2.3cm
breadboards: 1

parts:
  Part1 = Adafruit QT Py RP2040 [part_number="Adafruit #4900"]  # not connected
  Pad33 = Pad [width=3 height=1.75 connect=center]
  10uF_1206 = Ceramic Capacitor [capacitance=1µF package="1206 [SMD, multilayer]"]
  u_FL = U.FL [package=u.fl]
  Pad34 = Pad [width=3 height=1.75 connect=center]
  Pad35 = Pad [width=3 height=1.75 connect=center]
  Pad36 = Pad [width=3 height=1.75 connect=center]
  Pad37 = Pad [width=3 height=1.75 connect=center]  # not connected
  Pad38 = Pad [width=3 height=1.75 connect=center]
  Pad39 = Pad [width=3 height=1.75 connect=center]
  Pad40 = Pad [width=3 height=1.75 connect=center]
  Pad41 = Pad [width=3 height=1.75 connect=center]
  J3 = female pin header, 6 pins [form="♀ (female)"]
  J4 = female pin header, 4 pins [form="♀ (female)"]
  Ant = female pin header, 1 pin [form="♀ (female)"]
  Part2 = Adafruit LiPoly Charger BFF for QT Py [part_number="Adafruit #5397"]  # not connected
  Pad42 = Pad [width=1 height=2.75 connect=center]
  Pad43 = Pad [width=1 height=2.75 connect=center]
  Pad44 = Pad [width=1 height=2.75 connect=center]
  Pad45 = Pad [width=1 height=2.75 connect=center]
  Pad46 = Pad [width=1 height=2.75 connect=center]
  Pad47 = Pad [width=1 height=2.75 connect=center]
  Pad48 = Pad [width=1 height=2.75 connect=center]
  Pad49 = Pad [width=1 height=2.75 connect=center]
  Pad50 = Pad [width=1 height=2.75 connect=center]
  Pad51 = Pad [width=1 height=2.75 connect=center]
  Pad52 = Pad [width=1 height=2.75 connect=center]

nets:
  N1: Pad33.pad, J4.pin1, Pad50.pad
  N2: 10uF_1206.0, u_FL.GND, Pad36.pad, J3.pin1, Pad43.pad, Pad47.pad, Pad52.pad
  N3: 10uF_1206.1, Pad34.pad, J3.pin2, Pad44.pad
  N4: u_FL.SIGNAL, Ant.pin1, Pad42.pad
  N5: Pad35.pad, J3.pin5, Pad48.pad
  N6: Pad38.pad, J3.pin4, Pad49.pad
  N7: Pad39.pad, J3.pin6, Pad46.pad
  N8: Pad40.pad, J4.pin3, Pad45.pad
  N9: Pad41.pad, J4.pin2, Pad51.pad

notes:
  SCK
  MOSI
  MISO
  GND
  3V3
  RFMX9HCW
  QT/XIAO
  Backpack v1
  RESET
  CS
  Ant
  IRQ
  v1
  QT
  BP

custom parts:
  Adafruit QT Py RP2040: Description What a cutie pie! Or is it... a QT Py? This diminutive dev board comes with one of our new favorite chip, the RP2040. It's been made famous in the new Raspberry Pi Pico and our Feather RP2040 and ItsyBitsy RP2040, but what if we wanted something really smol? A new chip means a new QT Py, and the Raspberry Pi RP2040 is no exception. When we saw this chip we thought "this chip is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
  U.FL: SMD antenna connector- WRL-09144
  Adafruit LiPoly Charger BFF for QT Py: Is your QT Py all alone, lacking a friend to travel the wide world with? When you were a kid you may have learned about the "buddy" system, well this product is kinda like that! A board that will watch your QT Py's back and give it the power and support to wander out past your USB port. This little lipo charger is designed to fit onto the back of any QT Py board, and make it easy for portable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
